# Fritzing sketch 4leds (saved by Fritzing 0.9.3b)
breadboards: 1

parts:
  Componente1 = Arduino Uno (Rev3)
  R1 = Resistor [tolerance=±5% resistance=220 package=THT]
  LED2 = LED - 5mm [color="Red (633nm)" package="5 mm [THT]"]
  R2 = Resistor [tolerance=±5% resistance=220 package=THT]
  LED3 = LED - 5mm [color="Red (633nm)" package="5 mm [THT]"]
  LED4 = LED - 5mm [color="Red (633nm)" package="5 mm [THT]"]
  LED5 = LED - 5mm [color="Red (633nm)" package="5 mm [THT]"]
  R3 = Resistor [tolerance=±5% resistance=220 package=THT]
  R4 = Resistor [tolerance=±5% resistance=220 package=THT]

nets:
  N1: Componente1.GND, LED2.cathode, LED3.cathode, LED4.cathode, LED5.cathode
  N2: Componente1.D4, R4.Pin_1
  N3: Componente1.D5_PWM, R3.Pin_1
  N4: Componente1.D6_PWM, R2.Pin_1
  N5: Componente1.D7, R1.Pin_1
  N6: R1.Pin_0, LED3.anode
  N7: LED2.anode, R2.Pin_0
  N8: LED4.anode, R3.Pin_0
  N9: LED5.anode, R4.Pin_0
