# Fritzing sketch 5leds (saved by Fritzing 0.9.3b)
breadboards: 1

parts:
  Componente1 = Arduino Uno (Rev3)
  R1 = Resistor [tolerance=±5% resistance=220 package=THT]
  LED2 = LED - 5mm [color="Red (633nm)" package="5 mm [THT]"]
  R2 = Resistor [tolerance=±5% resistance=220 package=THT]
  LED3 = LED - 5mm [color="Red (633nm)" package="5 mm [THT]"]
  LED4 = LED - 5mm [color="Red (633nm)" package="5 mm [THT]"]
  LED5 = LED - 5mm [color="Red (633nm)" package="5 mm [THT]"]
  R3 = Resistor [tolerance=±5% resistance=220 package=THT]
  R4 = Resistor [tolerance=±5% resistance=220 package=THT]
  LED6 = LED - 5mm [color="Red (633nm)" package="5 mm [THT]"]
  R5 = Resistor [tolerance=±5% resistance=220 package=THT]

nets:
  N1: Componente1.GND, LED2.cathode, LED3.cathode, LED4.cathode, LED5.cathode, LED6.cathode
  N2: Componente1.D2, R5.Pin_1
  N3: Componente1.D3_PWM, R4.Pin_1
  N4: Componente1.D4, R3.Pin_1
  N5: Componente1.D5_PWM, R2.Pin_1
  N6: Componente1.D6_PWM, R1.Pin_1
  N7: R1.Pin_0, LED3.anode
  N8: LED2.anode, R2.Pin_0
  N9: LED4.anode, R3.Pin_0
  N10: LED5.anode, R4.Pin_0
  N11: LED6.anode, R5.Pin_0
