# Fritzing sketch 2ledsPWM (saved by Fritzing 0.9.3b)
breadboards: 1

parts:
  Componente1 = Arduino Uno (Rev3)
  LED2 = LED - 5mm [color="Red (633nm)" package="5 mm [THT]"]
  R2 = Resistor [tolerance=±5% resistance=220 package=THT]
  LED4 = LED - 5mm [color="Red (633nm)" package="5 mm [THT]"]
  R3 = Resistor [tolerance=±5% resistance=220 package=THT]

nets:
  N1: Componente1.GND, LED2.cathode, LED4.cathode
  N2: Componente1.D3_PWM, R3.Pin_1
  N3: Componente1.D5_PWM, R2.Pin_1
  N4: LED2.anode, R2.Pin_0
  N5: LED4.anode, R3.Pin_0
