# Fritzing sketch p072 (saved by Fritzing 0.9.3b)
breadboards: 1

parts:
  R1 = Rotary Potentiometer (Small) [maximum_resistance=100kΩ package=THT]
  Componente1 = Arduino Uno (Rev3)
  R2 = Resistor [tolerance=±5% resistance=220 package=THT]
  LED1 = LED - 5mm [color="Red (633nm)" package="5 mm [THT]"]

nets:
  N1: R1.leg1, Componente1.GND, LED1.cathode
  N2: R1.wiper, Componente1.A0
  N3: Componente1.D3_PWM, R2.Pin_1
  N4: R2.Pin_0, LED1.anode
