# Fritzing sketch p073 (saved by Fritzing 0.9.3b)
breadboards: 1

parts:
  Componente1 = Arduino Uno (Rev3)
  R3 = Photocell (LDR) [package=THT]
  R4 = Resistor [tolerance=±5% resistance=10k package=THT]

nets:
  N1: Componente1.A0, R3.pin_0, R4.Pin_1
  N2: Componente1.5V, R4.Pin_0
  N3: Componente1.GND, R3.pin_1
