# Fritzing sketch servo5 (saved by Fritzing 0.9.3b)
breadboards: 1

parts:
  Parte1 = Arduino Uno (Rev3)
  J1 = Basic Servo
  Parte2 = Thumb Joystick
  J2 = Basic Servo

nets:
  N1: Parte1.A0, Parte2.HORZ
  N2: Parte1.A1, Parte2.VERT
  VCC: Parte1.5V, J1.vcc, Parte2.VCC, J2.vcc
  GND: Parte1.GND, J1.gnd, Parte2.GND, J2.gnd
