# Fritzing sketch ir (saved by Fritzing 0.9.3b)
breadboards: 1

parts:
  Parte1 = Arduino Uno (Rev3)
  IR1 = TSOP312.., 314.. [package=THT]

nets:
  N1: Parte1.D11_PWM/MOSI, IR1.GND
  N2: Parte1.5V, IR1.Data
  N3: Parte1.GND, IR1.Vs
