# Fritzing sketch ir_lcd (saved by Fritzing 0.9.3b)
breadboards: 1

parts:
  Parte1 = Arduino Uno (Rev3)
  IR1 = TSOP312.., 314.. [package=THT]
  LCM1602_IIC1 = LCM1602 IIC [part_number="LCM1602 IIC" chip_label="LCM1602 IIC" package="DIP (Dual Inline) [THT]"]
  LCD1 = LCD screen  # not connected

nets:
  N1: Parte1.A4/SDA, LCM1602_IIC1.SDA
  N2: Parte1.D11_PWM/MOSI, IR1.GND
  5V: Parte1.5V, IR1.Data, LCM1602_IIC1.VCC
  GND: Parte1.GND, IR1.Vs, LCM1602_IIC1.GND

custom parts:
  LCM1602 IIC: I2C-Module to use a 1602 or 2004 LCD on with the wire.h libory Serial LCD Modul
