# Fritzing sketch p16 (saved by Fritzing 0.9.3b)
breadboards: 1

parts:
  Componente1 = Bluetooth HC-06
  Componente2 = Arduino Uno (Rev3)

nets:
  N1: Componente1.RXD, Componente2.D2
  N2: Componente1.TXD, Componente2.D3_PWM
  GND: Componente1.GND, Componente2.GND
  VCC: Componente1.VCC, Componente2.5V
