# Fritzing sketch p16_dht11 (saved by Fritzing 0.9.3b)
breadboards: 1

parts:
  Componente1 = Bluetooth HC-06
  Componente2 = Arduino Uno (Rev3)
  DHT1 = DHT11 Humitidy and Temperature Sensor

nets:
  N1: Componente1.RXD, Componente2.D2
  N2: Componente1.TXD, Componente2.D3_PWM
  GND: Componente1.GND, Componente2.GND, DHT1.GND
  VCC: Componente1.VCC, Componente2.5V, DHT1.VDD
  N3: Componente2.D7, DHT1.DATA

custom parts:
  DHT11 Humitidy and Temperature Sensor: DHT11 Humidity and Temperature Sensor
