# Fritzing sketch p16_rele (saved by Fritzing 0.9.3b)
breadboards: 1

parts:
  Componente1 = Bluetooth HC-06
  Componente2 = Arduino Uno (Rev3)
  KY-1 = Keyes Relay [package=THT]

nets:
  N1: Componente1.RXD, Componente2.D2
  N2: Componente1.TXD, Componente2.D3_PWM
  GND: Componente1.GND, Componente2.GND, KY-1.ground
  VCC: Componente1.VCC, Componente2.5V, KY-1.power
  N3: Componente2.D8, KY-1.signal

custom parts:
  Keyes Relay: The Keyes 5V relay module is suitable for SCM development, home appliance control. It uses a 5V~12V TIL control signal which can control DC / AC signal.
