# Fritzing sketch 2 buttons led (saved by Fritzing 0.9.2b)
breadboards: 1

parts:
  R1 = Resistor [tolerance=±5% resistance=10k package=THT]
  S1 = Pushbutton [package="[THT]"]  # not connected
  Parte1 = Arduino Uno (Rev3)
  R2 = Resistor [tolerance=±5% resistance=220 package=THT]
  LED1 = LED - 5mm [color="Red (633nm)" package="5 mm [THT]"]
  R3 = Resistor [tolerance=±5% resistance=10k package=THT]
  S2 = Pushbutton [package="[THT]"]  # not connected

nets:
  N1: R1.Pin_0, Parte1.GND, LED1.cathode, R3.Pin_0
  N2: R1.Pin_1, Parte1.D11_PWM/MOSI
  N3: Parte1.D10_PWM/SS, R3.Pin_1
  N4: Parte1.D3_PWM, R2.Pin_1
  N5: R2.Pin_0, LED1.anode
