# Fritzing sketch LP54 (saved by Fritzing 0.9.2b)
breadboards: 1

parts:
  Parte1 = Breakout Board for Electret Microphone
  Parte2 = Arduino Uno (Rev3)
  R1 = Resistor [tolerance=±5% resistance=220 package=THT]
  LED1 = LED - 5mm [color="Red (633nm)" package="5 mm [THT]"]

nets:
  VCC: Parte1.VCC, Parte2.5V
  GND: Parte1.GND, Parte2.GND, LED1.cathode
  N1: Parte1.AUD, Parte2.D8
  N2: Parte2.D3_PWM, R1.Pin_1
  N3: R1.Pin_0, LED1.anode
