# Fritzing sketch button led arduino (saved by Fritzing 0.9.2b)
breadboards: 1

parts:
  R1 = Resistor [tolerance=±5% resistance=10k package=THT]
  S1 = Pushbutton [package="[THT]"]
  Parte1 = Arduino Uno (Rev3)
  R2 = Resistor [tolerance=±5% resistance=220 package=THT]
  LED1 = LED - 5mm [color="Red (633nm)" package="5 mm [THT]"]

nets:
  N1: R1.Pin_0, S1.Pin_1, S1.Pin_2, Parte1.GND, LED1.cathode
  N2: R1.Pin_1, S1.Pin_3, S1.Pin_4, Parte1.D2
  N3: Parte1.D3_PWM, R2.Pin_1
  N4: R2.Pin_0, LED1.anode
