# Fritzing sketch keypad relay lcd password (saved by Fritzing 0.9.2b)
breadboards: 1

parts:
  KEYPAD1 = Membrane Matrix Keypad
  Parte1 = Arduino Uno (Rev3)
  LCD1 = LCD screen
  LCM1602_IIC1 = LCM1602 IIC [part_number="LCM1602 IIC" chip_label="LCM1602 IIC" package="DIP (Dual Inline) [THT]"]
  KY-4 = Keyes Relay [package=THT]

nets:
  N1: KEYPAD1.1, Parte1.D11_PWM/MOSI
  N2: KEYPAD1.2, Parte1.D10_PWM/SS
  N3: KEYPAD1.3, Parte1.D9_PWM
  N4: KEYPAD1.4, Parte1.D8
  N5: KEYPAD1.5, Parte1.D7
  N6: KEYPAD1.6, Parte1.D6_PWM
  N7: KEYPAD1.7, Parte1.D5_PWM
  N8: Parte1.A4/SDA, LCM1602_IIC1.SDA
  N9: Parte1.A5/SCL, LCM1602_IIC1.SCL
  N10: Parte1.D2, KY-4.signal
  5V: Parte1.5V, LCM1602_IIC1.VCC, KY-4.power
  GND: Parte1.GND, LCD1.VSS, LCM1602_IIC1.VSS, LCM1602_IIC1.GND, KY-4.ground
  VDD: LCD1.VDD, LCM1602_IIC1.VDD
  N11: LCD1.V0, LCM1602_IIC1.V0
  N12: LCD1.RS, LCM1602_IIC1.RS
  N13: LCD1.R/W, LCM1602_IIC1.RW
  N14: LCD1.E, LCM1602_IIC1.E
  N15: LCD1.DB0, LCM1602_IIC1.D0
  N16: LCD1.DB1, LCM1602_IIC1.D1
  N17: LCD1.DB2, LCM1602_IIC1.D2
  N18: LCD1.DB3, LCM1602_IIC1.D3
  N19: LCD1.DB4, LCM1602_IIC1.D4
  N20: LCD1.DB5, LCM1602_IIC1.D5
  N21: LCD1.DB6, LCM1602_IIC1.D6
  N22: LCD1.DB7, LCM1602_IIC1.D7
  N23: LCD1.LED+, LCM1602_IIC1.A
  N24: LCD1.LED-, LCM1602_IIC1.K

custom parts:
  Membrane Matrix Keypad: Membrane Matrix 3x4 Keypad
  LCM1602 IIC: I2C-Module to use a 1602 or 2004 LCD on with the wire.h libory Serial LCD Modul
  Keyes Relay: The Keyes 5V relay module is suitable for SCM development, home appliance control. It uses a 5V~12V TIL control signal which can control DC / AC signal.
