# Fritzing sketch keypas relay (saved by Fritzing 0.9.3b)
breadboards: 1

parts:
  KEYPAD1 = Membrane Matrix Keypad
  Parte1 = Arduino Uno (Rev3)
  KY-1 = Keyes Relay [package=THT]

nets:
  N1: KEYPAD1.1, Parte1.D11_PWM/MOSI
  N2: KEYPAD1.2, Parte1.D10_PWM/SS
  N3: KEYPAD1.3, Parte1.D9_PWM
  N4: KEYPAD1.4, Parte1.D8
  N5: KEYPAD1.5, Parte1.D7
  N6: KEYPAD1.6, Parte1.D6_PWM
  N7: KEYPAD1.7, Parte1.D5_PWM
  N8: Parte1.D2, KY-1.signal
  N9: Parte1.5V, KY-1.power
  N10: Parte1.GND, KY-1.ground

custom parts:
  Membrane Matrix Keypad: Membrane Matrix 3x4 Keypad
  Keyes Relay: The Keyes 5V relay module is suitable for SCM development, home appliance control. It uses a 5V~12V TIL control signal which can control DC / AC signal.
