# Fritzing sketch ldr realy pot (saved by Fritzing 0.9.2b)
breadboards: 1

parts:
  Parte1 = Arduino Uno (Rev3)
  R1 = Photocell (LDR) [package=THT]
  R2 = Resistor [tolerance=±5% resistance=10k package=THT]
  R3 = Rotary Potentiometer (Small) [maximum_resistance=100kΩ package=THT]
  KY-4 = Keyes Relay [package=THT]

nets:
  N1: Parte1.A0, R1.pin_0, R2.Pin_1
  N2: Parte1.A1, R3.wiper
  N3: Parte1.D8, KY-4.signal
  N4: Parte1.5V, R1.pin_1, R3.leg2, KY-4.power
  N5: Parte1.GND, R2.Pin_0, R3.leg1

custom parts:
  Keyes Relay: The Keyes 5V relay module is suitable for SCM development, home appliance control. It uses a 5V~12V TIL control signal which can control DC / AC signal.
