# Fritzing sketch ldr (saved by Fritzing 0.9.3b)
breadboards: 1

parts:
  Parte1 = Arduino Uno (Rev3)
  R1 = Photocell (LDR) [package=THT]
  R2 = Resistor [tolerance=±5% resistance=10k package=THT]

nets:
  N1: Parte1.A0, R1.pin_0, R2.Pin_1
  N2: Parte1.GND, R2.Pin_0
  N3: Parte1.5V, R1.pin_1
