# Fritzing sketch led (saved by Fritzing 0.9.2b)
breadboards: 1

parts:
  Parte1 = Arduino Uno (Rev3)
  R2 = Resistor [tolerance=±5% resistance=220 package=THT]
  LED1 = LED - 5mm [color="Red (633nm)" package="5 mm [THT]"]

nets:
  N1: Parte1.GND, LED1.cathode
  N2: Parte1.D3_PWM, R2.Pin_1
  N3: R2.Pin_0, LED1.anode
