# Fritzing sketch pasoapaso (saved by Fritzing 0.9.2b)

parts:
  Parte1 = Arduino Uno (Rev3)
  X1 = X113647 Stepper Driver Board [package=board]
  MOTOR1 = 28BYJ-48 Stepper Motor  # not connected

nets:
  N1: Parte1.D2, X1.IN1
  N2: Parte1.D3_PWM, X1.IN2
  N3: Parte1.D4, X1.IN3
  N4: Parte1.D5_PWM, X1.IN4

custom parts:
  X113647 Stepper Driver Board: A common stepper motor driver board based on ULN2003APG darlington array
