# Fritzing sketch secuencias pwm (saved by Fritzing 0.9.2b)
breadboards: 1

parts:
  R1 = Resistor [tolerance=±5% resistance=220 package=THT]
  LED1 = LED - 5mm [color="Red (633nm)" package="5 mm [THT]"]
  LED2 = LED - 5mm [color="Red (633nm)" package="5 mm [THT]"]  # not connected
  R2 = Resistor [tolerance=±5% resistance=220 package=THT]
  LED3 = LED - 5mm [color="Red (633nm)" package="5 mm [THT]"]
  R3 = Resistor [tolerance=±5% resistance=220 package=THT]
  Parte1 = Arduino Uno (Rev3)

nets:
  N1: R1.Pin_0, LED1.anode
  N2: R1.Pin_1, Parte1.D11_PWM/MOSI
  N3: LED1.cathode, LED3.cathode, Parte1.GND
  N4: R2.Pin_1, Parte1.D10_PWM/SS
  N5: LED3.anode, R3.Pin_0
  N6: R3.Pin_1, Parte1.D9_PWM
